# Fritzing sketch Part_1_Flash_LED (saved by Fritzing 0.3.19b)
breadboards: 1

parts:
  Arduino1 = Arduino
  LED1 = Red LED - 5mm
  R1 = Resistor [resistance=220 package=THT]

nets:
  N1: Arduino1.GND, R1.Pin_1
  N2: Arduino1.D0RX, LED1.anode
  N3: LED1.cathode, R1.Pin_0
