# Fritzing sketch Part_2_Basic_Traffic_Lights (saved by Fritzing 0.3.19b)
breadboards: 1

parts:
  Arduino1 = Arduino
  LED1_(R) = Red LED - 5mm
  R1 = Resistor [resistance=220 package=THT]
  LED2_(Y) = yellow LED - 5mm
  LED3 = green LED - 5mm
  R2 = Resistor [resistance=220 package=THT]
  R3 = Resistor [resistance=220 package=THT]

nets:
  N1: Arduino1.GND, R1.Pin_1, R2.Pin_1, R3.Pin_1
  N2: Arduino1.D2, LED3.anode
  N3: Arduino1.D1TX, LED2_(Y).anode
  N4: Arduino1.D0RX, LED1_(R).anode
  N5: LED1_(R).cathode, R1.Pin_0
  N6: LED2_(Y).cathode, R2.Pin_0
  N7: LED3.cathode, R3.Pin_0
