# Fritzing sketch Part_4_Beeping_Pedestrian_Crossing (saved by Fritzing 0.3.19b)
breadboards: 1

parts:
  Arduino1 = Arduino
  LED1 = Red LED - 5mm
  R1 = Resistor [resistance=220 package=THT]
  LED2 = yellow LED - 5mm
  LED3 = green LED - 5mm
  R2 = Resistor [resistance=220 package=THT]
  R3 = Resistor [resistance=220 package=THT]
  LED4 = Red LED - 5mm
  S1 = Pushbutton [package="[THT]"]
  LED5 = green LED - 5mm
  R4 = Resistor [resistance=220 package=THT]
  R5 = Resistor [resistance=220 package=THT]
  R6 = Resistor [resistance=220 package=THT]
  J1 = Piezo Speaker

nets:
  N1: Arduino1.GND, Arduino1.D8, R1.Pin_1, R2.Pin_1, R3.Pin_1, R4.Pin_1, R5.Pin_1, R6.Pin_1, J1.pin1, J1.pin2
  N2: Arduino1.D7, S1.Pin_3, S1.Pin_4, R6.Pin_0
  N3: Arduino1.D6, LED5.anode
  N4: Arduino1.D5, LED4.anode
  N5: Arduino1.D4, LED3.anode
  N6: Arduino1.D3, LED2.anode
  N7: Arduino1.D2, LED1.anode
  N8: Arduino1.+5V, S1.Pin_1, S1.Pin_2
  N9: LED1.cathode, R1.Pin_0
  N10: LED2.cathode, R2.Pin_0
  N11: LED3.cathode, R3.Pin_0
  N12: LED4.cathode, R4.Pin_0
  N13: LED5.cathode, R5.Pin_0
